// Logisim project cla_4bit.circ as structural Verilog: 1 circuit, main circuit main
module main (
  input  C0,
  input  A1,
  input  B1,
  input  A2,
  input  B2,
  input  A3,
  input  B3,
  input  A4,
  input  B4,
  output out_10,
  output out_11,
  output out_12,
  output out_13,
  output out_14
);

  wire and_1_out, and_2_out, and_3_out, and_4_out, and_5_out, and_6_out, and_7_out, and_8_out, and_9_out,
       and_10_out, C1_out, C2_out, C3_out, G1_out, G2_out, G3_out, G4_out, P1_out, P2_out, P3_out, P4_out;

  and G1 (G1_out, A1, B1);
  xor P1 (P1_out, A1, B1);
  and G2 (G2_out, A2, B2);
  xor P2 (P2_out, A2, B2);
  and G3 (G3_out, A3, B3);
  xor P3 (P3_out, A3, B3);
  and G4 (G4_out, A4, B4);
  xor P4 (P4_out, A4, B4);
  and and_1 (and_1_out, G1_out, P2_out);
  and and_2 (and_2_out, C0, P1_out, P2_out);
  and and_3 (and_3_out, G2_out, P3_out);
  and and_4 (and_4_out, P3_out, P2_out, G1_out);
  and and_5 (and_5_out, P1_out, P2_out, P3_out, C0);
  and and_6 (and_6_out, G3_out, P4_out);
  and and_7 (and_7_out, P4_out, P3_out, G2_out);
  and and_8 (and_8_out, P4_out, P3_out, P2_out, G1_out);
  and and_9 (and_9_out, P4_out, P3_out, P2_out, P1_out, C0);
  and and_10 (and_10_out, C0, P1_out);
  or C1 (C1_out, G1_out, and_10_out);
  or C2 (C2_out, G2_out, and_1_out, and_2_out);
  or C3 (C3_out, G3_out, and_3_out, and_4_out, and_5_out);
  xor S1 (out_10, C0, P1_out);
  xor S2 (out_11, C1_out, P2_out);
  xor S3 (out_12, C2_out, P3_out);
  xor S4 (out_13, C3_out, P4_out);
  or C4 (out_14, G4_out, and_6_out, and_7_out, and_8_out, and_9_out);
endmodule
