// Logisim project full_adder.circ as structural Verilog: 1 circuit, main circuit main
module main (
  input  A,
  input  B,
  input  Cin,
  output out_4,
  output out_5
);

  wire C1_out, C2_out, S1_out;

  and C1 (C1_out, A, B);
  xor S1 (S1_out, A, B);
  and C2 (C2_out, S1_out, Cin);
  or Cout (out_4, C1_out, C2_out);
  xor S (out_5, S1_out, Cin);
endmodule
