// Logisim project hello_and.circ as structural Verilog: 1 circuit, main circuit main
module main (
  input  A,
  input  B,
  output C,
  output S
);

  and and_1 (C, A, B);
  xor xor_1 (S, A, B);
endmodule
