// Logisim project sub_circut.circ as structural Verilog: 3 circuits, main circuit main
module main (
  input  Cin,
  input  A1,
  input  A2,
  input  A3,
  input  A4,
  input  B1,
  input  B2,
  input  B3,
  input  B4,
  output out_10,
  output out_11,
  output out_12,
  output out_13,
  output out_14,
  output out_15,
  output out_16,
  output out_17,
  output out_18,
  output out_19
);

  FullAdder fulladder_1 (
    .Cin(Cin), .A1(A1), .B1(B1), .A2(A2), .B2(B2), .A3(A3), .B3(B3), .A4(A4), .B4(B4), .S1(out_10),
    .S2(out_11), .S3(out_12), .S4(out_13), .Cout(out_14));
  CLA cla_1 (
    .Cin(Cin), .A1(A1), .B1(B1), .A2(A2), .B2(B2), .A3(A3), .B3(B3), .A4(A4), .B4(B4), .S1(out_15),
    .S2(out_16), .S3(out_17), .S4(out_18), .Cout(out_19));
endmodule

module FullAdder (
  input  Cin,
  input  A1,
  input  B1,
  input  A2,
  input  B2,
  input  A3,
  input  B3,
  input  A4,
  input  B4,
  output S1,
  output S2,
  output S3,
  output S4,
  output Cout
);

  wire adder_1_cout, adder_2_cout, adder_3_cout;

  Adder #(.width(1)) adder_1 (.a(A1), .b(B1), .out(S1), .cin(Cin), .cout(adder_1_cout));
  Adder #(.width(1)) adder_2 (.a(A2), .b(B2), .out(S2), .cin(adder_1_cout), .cout(adder_2_cout));
  Adder #(.width(1)) adder_3 (.a(A3), .b(B3), .out(S3), .cin(adder_2_cout), .cout(adder_3_cout));
  Adder #(.width(1)) adder_4 (.a(A4), .b(B4), .out(S4), .cin(adder_3_cout), .cout(Cout));
endmodule

module CLA (
  input  Cin,
  input  A1,
  input  B1,
  input  A2,
  input  B2,
  input  A3,
  input  B3,
  input  A4,
  input  B4,
  output S1,
  output S2,
  output S3,
  output S4,
  output Cout
);

  wire and_1_out, and_2_out, and_3_out, and_4_out, and_5_out, and_6_out, and_7_out, and_8_out, and_9_out,
       and_10_out, C1_out, C2_out, C3_out, G1_out, G2_out, G3_out, G4_out, P1_out, P2_out, P3_out, P4_out;

  and G1 (G1_out, A1, B1);
  xor P1 (P1_out, A1, B1);
  and G2 (G2_out, A2, B2);
  xor P2 (P2_out, A2, B2);
  and G3 (G3_out, A3, B3);
  xor P3 (P3_out, A3, B3);
  and G4 (G4_out, A4, B4);
  xor P4 (P4_out, A4, B4);
  and and_1 (and_1_out, G1_out, P2_out);
  and and_2 (and_2_out, Cin, P1_out, P2_out);
  and and_3 (and_3_out, G2_out, P3_out);
  and and_4 (and_4_out, P3_out, P2_out, G1_out);
  and and_5 (and_5_out, P1_out, P2_out, P3_out, Cin);
  and and_6 (and_6_out, G3_out, P4_out);
  and and_7 (and_7_out, P4_out, P3_out, G2_out);
  and and_8 (and_8_out, P4_out, P3_out, P2_out, G1_out);
  and and_9 (and_9_out, P4_out, P3_out, P2_out, P1_out, Cin);
  and and_10 (and_10_out, Cin, P1_out);
  or C1 (C1_out, G1_out, and_10_out);
  or C2 (C2_out, G2_out, and_1_out, and_2_out);
  or C3 (C3_out, G3_out, and_3_out, and_4_out, and_5_out);
  xor xor_1 (S1, Cin, P1_out);
  xor xor_2 (S2, C1_out, P2_out);
  xor xor_3 (S3, C2_out, P3_out);
  xor xor_4 (S4, C3_out, P4_out);
  or C4 (Cout, G4_out, and_6_out, and_7_out, and_8_out, and_9_out);
endmodule
